# Fritzing sketch sketch (saved by Fritzing 1.0.6)
breadboards: 1

parts:
  Raspberry_Pi1 = Raspberry Pi B+
  Adafruit#1 = Adafruit ADS1115 16-Bit ADC [part_number=1085]
  KY-1 = KY-039 Heartbeat Sensor [part_number=KY-039]
  KY-2 = KY-016 3-Color RGB LED Module [part_number="RGB Status LED"]
  KY-3 = KY-006 Passive Buzzer Module [part_number=KY-006]
  KY-4 = KY-015 DHT11 Temperature and Humidity Sensor [part_number=KY-015]
  KY-5 = KY-001 DS18B20 Temperature Sensor [part_number=KY-001]

nets:
  3V3: Raspberry_Pi1.3v3, Adafruit#1.VCC, KY-1.+, KY-4.+, KY-5.+
  N1: Raspberry_Pi1.GPIO2, Adafruit#1.SDA
  N2: Raspberry_Pi1.GPIO3, Adafruit#1.SCL
  N3: Raspberry_Pi1.GPIO4, KY-5.S
  N4: Raspberry_Pi1.GPIO17, KY-4.S
  N5: Raspberry_Pi1.GPIO22, KY-2.R
  GND: Raspberry_Pi1.GND, Adafruit#1.GND, KY-1.-, KY-2.-, KY-3.-, KY-4.-, KY-5.-
  N6: Raspberry_Pi1.GPIO24, KY-2.B
  N7: Raspberry_Pi1.GPIO23, KY-2.G
  N8: Raspberry_Pi1.GPIO18, KY-3.S
  N9: Adafruit#1.AIN0, KY-1.S

custom parts:
  KY-039 Heartbeat Sensor: KY-039 heartbeat/pulse sensor module commonly included in 37-in-1 sensor kits. Pin order is S, +, -.
  KY-016 3-Color RGB LED Module: KY-016 3-color RGB LED module. Common cathode pin is marked -; drive R, G, and B individually.
  KY-006 Passive Buzzer Module: KY-006 passive piezo buzzer module. Drive S with a square wave or tone output; the middle header pin is typically not connected; - is GND.
  KY-015 DHT11 Temperature and Humidity Sensor: KY-015 DHT11 temperature and humidity sensor module. Pin order is S, +, - on common Keyes-style modules; always confirm the silkscreen on your board.
  KY-001 DS18B20 Temperature Sensor: KY-001 DS18B20 1-Wire digital temperature sensor module. Pin order is S, +, - on common Keyes-style modules; always confirm the silkscreen on your board.
